# Fritzing sketch main sticker (saved by Fritzing 0.9.3b)
perfboards: 2

parts:
  R1 = Resistor [tolerance=±5% resistance=220 package=THT]
  LED3 = LED - 5mm [color="Red (633nm)" package="5 mm [THT]"]
  LED5 = LED - 5mm [color="Red (633nm)" package="5 mm [THT]"]
  R2 = Resistor [tolerance=±5% resistance=220 package=THT]  # not connected
  LED4 = LED - 3mm [color="White (4500K)" package="3 mm [THT]"]
  LED2 = LED - 3mm [color="White (4500K)" package="3 mm [THT]"]
  LED1 = LED - 3mm [color="White (4500K)" package="3 mm [THT]"]
  Part1 = Arduino Uno (Rev3)
  Part2 = Bluetooth HC-05 Macho
  M2 = DC Motor
  M3 = DC Motor
  BAT1 = Battery Holders [package=lipo-1100mAh]
  S1 = Toggle Switch [package=THT]
  M1 = L293D Motor Driver

nets:
  N1: R1.Pin_0, LED1.cathode
  GND: R1.Pin_1, Part1.GND, Part2.GND, M1.pin_4
  N2: LED3.cathode, LED5.cathode
  N3: LED3.anode, LED5.anode
  N4: LED4.anode, Part1.D8
  N5: LED2.anode, LED1.anode, Part1.D6_PWM
  N6: Part1.D0/RX, Part2.TXD
  N7: Part1.D1/TX, Part2.RXD
  N8: Part1.D2, M1.pin_8
  N9: Part1.D3_PWM, M1.pin_7
  N10: Part1.D4, M1.pin_6
  N11: Part1.D5_PWM, M1.pin_5
  5V: Part1.5V, Part2.VCC
  N12: Part1.VIN, M1.pin_3
  N13: M2.pin_1, M1.pin_11
  N14: M2.pin_2, M1.pin_12
  N15: M3.pin_1, M1.pin_9
  N16: M3.pin_2, M1.pin_10
  N17: BAT1.+, S1.COM, S1.L2
